# Fritzing sketch IRBeaconLargeLM317 (saved by Fritzing 0.9.3b)
circuit board: 15.4371cm x 1.59911cm
breadboards: 1

parts:
  LED1 = LED - 5mm [color="Red (633nm)" package="5 mm [THT]"]
  LED3 = LED - 5mm [color="Red (633nm)" package="5 mm [THT]"]
  LED5 = LED - 5mm [color="Red (633nm)" package="5 mm [THT]"]
  LED6 = LED - 5mm [color="Red (633nm)" package="5 mm [THT]"]
  J1 = Screw terminal - 2 pins [package=THT]
  U1 = Voltage Regulator [package=to220-adj]
  R1 = Resistor [tolerance=±5% resistance=25 package=THT]
  C1 = Ceramic Capacitor [capacitance=100nF package="100 mil [THT, multilayer]"]
  C2 = Electrolytic Capacitor [capacitance=10µF package="100 mil [THT, electrolytic]"]
  C3 = Electrolytic Capacitor [capacitance=47µF package="100 mil [THT, electrolytic]"]
  SW1 = female pin header, 3 pins [form="♀ (female)"]
  J2 = Screw terminal - 2 pins [package=THT]

nets:
  N1: LED1.cathode, LED3.anode
  N2: LED1.anode, U1.OUT, R1.Pin_1, C3.+
  N3: LED3.cathode, LED5.anode
  N4: LED5.cathode, LED6.anode
  N5: LED6.cathode, J1.pin2, C1.0, C2.-, C3.-, J2.pin2
  N6: J1.pin1, SW1.pin2
  N7: U1.ADJ, R1.Pin_0
  N8: U1.IN, C1.1, C2.+, SW1.pin3, J2.pin1

notes:
  I=1.25/R
  If = 50mA; Ifp = 80mA
  Vf = 1.4 - 1.6v
  Vin > 1.6*4+1.25=7.65
